// Digital circuit FULLADDER.dig as structural Verilog
module FULLADDER (
  input  B,
  input  A,
  input  Cin,
  output S,
  output Cout
);

  wire and_1_a_b, and_2_a_b, and_3_a_b, or_1_a_plus_b, xor_1_a_b;

  XOR xor_1 (.A(B), .B(Cin), .A_B(xor_1_a_b));
  AND and_1 (.A(B), .B(Cin), .A_B(and_1_a_b));
  AND and_2 (.A(B), .B(A), .A_B(and_2_a_b));
  AND and_3 (.A(A), .B(Cin), .A_B(and_3_a_b));
  XOR xor_2 (.A(A), .B(xor_1_a_b), .A_B(S));
  OR or_1 (.A(and_1_a_b), .B(and_2_a_b), .A_plus_B(or_1_a_plus_b));
  OR or_2 (.A(or_1_a_plus_b), .B(and_3_a_b), .A_plus_B(Cout));
endmodule
