// Digital circuit HALFADDER.dig as structural Verilog
module HALFADDER (
  input  A,
  input  B,
  output S,
  output Cout
);

  XOR xor_1 (.A(A), .B(B), .A_B(S));
  AND and_1 (.A(A), .B(B), .A_B(Cout));
endmodule
