// Digital circuit fullhalf45.dig as structural Verilog
module fullhalf45 (
  input  _01,
  input  _02,
  input  _03,
  input  _04,
  input  _10,
  input  _11,
  input  _12,
  input  _13,
  input  _14,
  output a,
  output s0,
  output s1,
  output s2,
  output s3,
  output Cout
);

  wire fulladder_1_cout, fulladder_2_cout, fulladder_3_cout, halfadder_1_cout;

  HALFADDER halfadder_1 (.A(_01), .B(_10), .S(a), .Cout(halfadder_1_cout));
  FULLADDER fulladder_1 (.B(_02), .A(_11), .Cin(halfadder_1_cout), .S(s0), .Cout(fulladder_1_cout));
  FULLADDER fulladder_2 (.B(_03), .A(_12), .Cin(fulladder_1_cout), .S(s1), .Cout(fulladder_2_cout));
  FULLADDER fulladder_3 (.B(_04), .A(_13), .Cin(fulladder_2_cout), .S(s2), .Cout(fulladder_3_cout));
  HALFADDER halfadder_2 (.A(fulladder_3_cout), .B(_14), .S(s3), .Cout(Cout));
endmodule
