// Digital circuit fullhalf55.dig as structural Verilog
module fullhalf55 (
  input  s0,
  input  s1,
  input  s2,
  input  s3,
  input  Cin,
  input  A0,
  input  A1,
  input  A2,
  input  A3,
  input  A4,
  output a,
  output s4,
  output s5,
  output s6,
  output s7,
  output Cout
);

  wire fulladder_1_cout, fulladder_2_cout, fulladder_3_cout, halfadder_1_cout;

  HALFADDER halfadder_1 (.A(s0), .B(A0), .S(a), .Cout(halfadder_1_cout));
  FULLADDER fulladder_1 (.B(s1), .A(A1), .Cin(halfadder_1_cout), .S(s4), .Cout(fulladder_1_cout));
  FULLADDER fulladder_2 (.B(s2), .A(A2), .Cin(fulladder_1_cout), .S(s5), .Cout(fulladder_2_cout));
  FULLADDER fulladder_3 (.B(s3), .A(A3), .Cin(fulladder_2_cout), .S(s6), .Cout(fulladder_3_cout));
  FULLADDER fulladder_4 (.B(Cin), .A(A4), .Cin(fulladder_3_cout), .S(s7), .Cout(Cout));
endmodule
