// Digital circuit main5Bits.dig as structural Verilog
module main5Bits (
  input  B3,
  input  B2,
  input  B1,
  input  B0,
  input  A4,
  input  A3,
  input  A2,
  input  A1,
  input  A0,
  input  B4,
  output a9,
  output a8,
  output a7,
  output a6,
  output a5,
  output a4_2,
  output a3_2,
  output a2_2,
  output a1_2,
  output a0_2
);

  Circuito5Bits circuito5bits_1 (
    .B4(B4), .B3(B3), .B2(B2), .B1(B1), .B0(B0), .A4(A4), .A3(A3), .A2(A2), .A1(A1), .A0(A0), .a9(a9),
    .a8(a8), .a7(a7), .a6(a6), .a5(a5), .a4_2(a4_2), .a3_2(a3_2), .a2_2(a2_2), .a1_2(a1_2), .a0_2(a0_2));
endmodule
