// Digital circuit mult5.dig as structural Verilog
module mult5 (
  input  B0,
  input  B1,
  input  B2,
  input  B3,
  input  B4,
  input  A,
  output A0,
  output A1,
  output A2,
  output A3,
  output A4
);

  AND and_1 (.A(A), .B(B0), .A_B(A0));
  AND and_2 (.A(A), .B(B1), .A_B(A1));
  AND and_3 (.A(A), .B(B2), .A_B(A2));
  AND and_4 (.A(A), .B(B3), .A_B(A3));
  AND and_5 (.A(A), .B(B4), .A_B(A4));
endmodule
