// Digital circuit AND.dig as structural Verilog
module AND (
  input  A,
  input  B,
  output A_B
);

  wire nor_1_out, nor_2_out;

  nor nor_1 (nor_1_out, A, A);
  nor nor_2 (nor_2_out, B, B);
  nor nor_3 (A_B, nor_1_out, nor_2_out);
endmodule
