// Digital circuit cores.dig as structural Verilog
module cores (
  input  Sa,
  input  Sb,
  output R,
  output Y,
  output G
);

  and and_1 (R, Sa, Sb);
  and and_2 (Y, Sa, ~Sb);  // And
  and and_3 (G, ~Sa, Sb);  // And
endmodule
