// Digital circuit Circuito5Bits.dig as structural Verilog
module Circuito5Bits (
  input  B4,
  input  B3,
  input  B2,
  input  B1,
  input  B0,
  input  A4,
  input  A3,
  input  A2,
  input  A1,
  input  A0,
  output a9,
  output a8,
  output a7,
  output a6,
  output a5,
  output a4_2,
  output a3_2,
  output a2_2,
  output a1_2,
  output a0_2
);

  wire fullhalf45_1_cout, fullhalf45_1_s0, fullhalf45_1_s1, fullhalf45_1_s2, fullhalf45_1_s3,
       fullhalf55_1_cout, fullhalf55_1_s4, fullhalf55_1_s5, fullhalf55_1_s6, fullhalf55_1_s7,
       fullhalf55_2_cout, fullhalf55_2_s4, fullhalf55_2_s5, fullhalf55_2_s6, fullhalf55_2_s7, mult5_1_a1,
       mult5_1_a2, mult5_1_a3, mult5_1_a4, mult5_2_a0, mult5_2_a1, mult5_2_a2, mult5_2_a3, mult5_2_a4,
       mult5_3_a0, mult5_3_a1, mult5_3_a2, mult5_3_a3, mult5_3_a4, mult5_4_a0, mult5_4_a1, mult5_4_a2,
       mult5_4_a3, mult5_4_a4, mult5_5_a0, mult5_5_a1, mult5_5_a2, mult5_5_a3, mult5_5_a4;

  mult5 mult5_1 (
    .B0(B0), .B1(B1), .B2(B2), .B3(B3), .B4(B4), .A(A0), .A0(a0_2), .A1(mult5_1_a1), .A2(mult5_1_a2),
    .A3(mult5_1_a3), .A4(mult5_1_a4));
  mult5 mult5_2 (
    .B0(B0), .B1(B1), .B2(B2), .B3(B3), .B4(B4), .A(A1), .A0(mult5_2_a0), .A1(mult5_2_a1), .A2(mult5_2_a2),
    .A3(mult5_2_a3), .A4(mult5_2_a4));
  mult5 mult5_3 (
    .B0(B0), .B1(B1), .B2(B2), .B3(B3), .B4(B4), .A(A2), .A0(mult5_3_a0), .A1(mult5_3_a1), .A2(mult5_3_a2),
    .A3(mult5_3_a3), .A4(mult5_3_a4));
  mult5 mult5_4 (
    .B0(B0), .B1(B1), .B2(B2), .B3(B3), .B4(B4), .A(A3), .A0(mult5_4_a0), .A1(mult5_4_a1), .A2(mult5_4_a2),
    .A3(mult5_4_a3), .A4(mult5_4_a4));
  mult5 mult5_5 (
    .B0(B0), .B1(B1), .B2(B2), .B3(B3), .B4(B4), .A(A4), .A0(mult5_5_a0), .A1(mult5_5_a1), .A2(mult5_5_a2),
    .A3(mult5_5_a3), .A4(mult5_5_a4));
  fullhalf45 fullhalf45_1 (
    ._01(mult5_1_a1), ._02(mult5_1_a2), ._03(mult5_1_a3), ._04(mult5_1_a4), ._10(mult5_2_a0),
    ._11(mult5_2_a1), ._12(mult5_2_a2), ._13(mult5_2_a3), ._14(mult5_2_a4), .a(a1_2), .s0(fullhalf45_1_s0),
    .s1(fullhalf45_1_s1), .s2(fullhalf45_1_s2), .s3(fullhalf45_1_s3), .Cout(fullhalf45_1_cout));
  fullhalf55 fullhalf55_1 (
    .s0(fullhalf45_1_s0), .s1(fullhalf45_1_s1), .s2(fullhalf45_1_s2), .s3(fullhalf45_1_s3),
    .Cin(fullhalf45_1_cout), .A0(mult5_3_a0), .A1(mult5_3_a1), .A2(mult5_3_a2), .A3(mult5_3_a3),
    .A4(mult5_3_a4), .a(a2_2), .s4(fullhalf55_1_s4), .s5(fullhalf55_1_s5), .s6(fullhalf55_1_s6),
    .s7(fullhalf55_1_s7), .Cout(fullhalf55_1_cout));
  fullhalf55 fullhalf55_2 (
    .s0(fullhalf55_1_s4), .s1(fullhalf55_1_s5), .s2(fullhalf55_1_s6), .s3(fullhalf55_1_s7),
    .Cin(fullhalf55_1_cout), .A0(mult5_4_a0), .A1(mult5_4_a1), .A2(mult5_4_a2), .A3(mult5_4_a3),
    .A4(mult5_4_a4), .a(a3_2), .s4(fullhalf55_2_s4), .s5(fullhalf55_2_s5), .s6(fullhalf55_2_s6),
    .s7(fullhalf55_2_s7), .Cout(fullhalf55_2_cout));
  fullhalf55 fullhalf55_3 (
    .s0(fullhalf55_2_s4), .s1(fullhalf55_2_s5), .s2(fullhalf55_2_s6), .s3(fullhalf55_2_s7),
    .Cin(fullhalf55_2_cout), .A0(mult5_5_a0), .A1(mult5_5_a1), .A2(mult5_5_a2), .A3(mult5_5_a3),
    .A4(mult5_5_a4), .a(a4_2), .s4(a5), .s5(a6), .s6(a7), .s7(a8), .Cout(a9));
endmodule
