// Digital circuit OR.dig as structural Verilog
module OR (
  input  A,
  input  B,
  output A_plus_B
);

  wire nor_1_out;

  nor nor_1 (nor_1_out, A, B);
  nor nor_2 (A_plus_B, nor_1_out, nor_1_out);
endmodule
