// Digital circuit XOR.dig as structural Verilog
module XOR (
  input  A,
  input  B,
  output A_B
);

  wire and_1_a_b, nor_1_out;

  AND and_1 (.A(A), .B(B), .A_B(and_1_a_b));
  nor nor_1 (nor_1_out, A, B);
  nor nor_2 (A_B, and_1_a_b, nor_1_out);
endmodule
