// Digital circuit TRABALHO.dig as structural Verilog
module TRABALHO (
  input  CLK,
  input  in_2,
  input  in_3
);

  wire D_out, jk_ff_1_q, rs_ff_as_1_q, semaforos_1_g2, semaforos_1_g13, semaforos_1_g45, semaforos_1_r,
       semaforos_1_r2, semaforos_1_r13, semaforos_1_r45, semaforos_1_y2, semaforos_1_y13;

  RS_FF_AS rs_ff_as_1 (.S(D_out), .R(semaforos_1_r), .Q(rs_ff_as_1_q));  // open: nQ
  JK_FF jk_ff_1 (.J(in_2), .C(CLK), .K(in_3), .Q(jk_ff_1_q));  // open: nQ
  semaforos semaforos_1 (
    .B(rs_ff_as_1_q), .CLK(jk_ff_1_q), .R13(semaforos_1_r13), .Y13(semaforos_1_y13), .G13(semaforos_1_g13),
    .R2(semaforos_1_r2), .Y2(semaforos_1_y2), .G2(semaforos_1_g2), .R45(semaforos_1_r45),
    .G45(semaforos_1_g45), .R(semaforos_1_r));
  LED led_1 (.in(semaforos_1_r13));
  LED led_2 (.in(semaforos_1_y13));
  LED led_3 (.in(semaforos_1_g13));
  LED led_4 (.in(semaforos_1_r2));
  LED led_5 (.in(semaforos_1_y2));
  LED led_6 (.in(semaforos_1_g2));
  LED led_7 (.in(semaforos_1_r13));
  LED led_8 (.in(semaforos_1_y13));
  LED led_9 (.in(semaforos_1_g13));
  LED led_10 (.in(semaforos_1_r45));
  LED led_11 (.in(semaforos_1_g45));
  LED led_12 (.in(semaforos_1_r45));
  LED led_13 (.in(semaforos_1_g45));
  Button D (.out(D_out));

  // Notes on the sheet:
  //   in_2: default 1
  //   in_3: default 1
endmodule
