// Digital circuit e0n+1.dig as structural Verilog
module e0n_1 (
  input  E0,
  input  nE1,
  input  nE2,
  input  B,
  output E0_n_plus_1
);

  wire and_1_out, and_2_out, and_3_out;

  and and_1 (and_1_out, B, ~E0);  // And
  and and_2 (and_2_out, ~B, E0, nE2);  // And
  and and_3 (and_3_out, nE1, B, nE2);
  or or_1 (E0_n_plus_1, and_1_out, and_2_out, and_3_out);
endmodule
