// Digital circuit e1n+1.dig as structural Verilog
module e1n_1 (
  input  B,
  input  E0,
  input  E1,
  input  E2,
  output E1_n_plus_1
);

  wire and_1_out, and_2_out, and_3_out;

  and and_1 (and_1_out, ~B, ~E0, ~E1, E2);  // And
  and and_2 (and_2_out, B, ~E0, E1);  // And
  and and_3 (and_3_out, E1, ~E2);  // And
  or or_1 (E1_n_plus_1, and_1_out, and_2_out, and_3_out);
endmodule
