// Digital circuit s1.dig as structural Verilog
module s1 (
  input  E1,
  input  E2,
  input  E0,
  output S1
);

  wire and_1_out, and_2_out;

  and and_1 (and_1_out, ~E0, ~E2);  // And
  and and_2 (and_2_out, E0, E2);
  or or_1 (S1, and_1_out, and_2_out, E1);
endmodule
