// Digital circuit s3.dig as structural Verilog
module s3 (
  input  nE1,
  input  nE2,
  input  E0,
  output S3
);

  wire and_1_out, and_2_out;

  and and_1 (and_1_out, ~E0, nE2);  // And
  and and_2 (and_2_out, E0, ~nE2);  // And
  or or_1 (S3, and_1_out, and_2_out, nE1);
endmodule
