// Digital circuit semaforos.dig as structural Verilog
module semaforos (
  input  B,
  input  CLK,
  output R13,
  output Y13,
  output G13,
  output R2,
  output Y2,
  output G2,
  output R45,
  output G45,
  output R
);

  wire E0_nq, E0_q, e0n_1_1_e0_n_plus_1, E1_nq, E1_q, e1n_1_1_e1_n_plus_1, E2_nq, E2_q, e2n_1_1_e2_n_plus_1,
       s0_1_s0, s1_1_s1, s2_1_s2, s3_1_s3, s4_1_s4;

  D_FF E0 (.D(e0n_1_1_e0_n_plus_1), .C(CLK), .Q(E0_q), .nQ(E0_nq));
  D_FF E1 (.D(e1n_1_1_e1_n_plus_1), .C(CLK), .Q(E1_q), .nQ(E1_nq));
  D_FF E2 (.D(e2n_1_1_e2_n_plus_1), .C(CLK), .Q(E2_q), .nQ(E2_nq));
  e0n_1 e0n_1_1 (.E0(E0_q), .nE1(E1_nq), .nE2(E2_nq), .B(B), .E0_n_plus_1(e0n_1_1_e0_n_plus_1));
  e1n_1 e1n_1_1 (.B(B), .E0(E0_q), .E1(E1_q), .E2(E2_q), .E1_n_plus_1(e1n_1_1_e1_n_plus_1));
  e2n_1 e2n_1_1 (.B(B), .E0(E0_q), .E2(E2_q), .E2_n_plus_1(e2n_1_1_e2_n_plus_1));
  s0 s0_1 (.E0(E0_q), .E1(E1_q), .E2(E2_q), .S0(s0_1_s0));
  s1 s1_1 (.E1(E1_q), .E2(E2_q), .E0(E0_q), .S1(s1_1_s1));
  s2 s2_1 (.E0(E0_q), .nE1(E1_nq), .E2(E2_q), .S2(s2_1_s2));
  s3 s3_1 (.nE1(E1_nq), .nE2(E2_nq), .E0(E0_q), .S3(s3_1_s3));
  s4 s4_1 (.nE0(E0_nq), .nE2(E2_nq), .S4(s4_1_s4));
  cores cores_1 (.Sa(s0_1_s0), .Sb(s1_1_s1), .R(R13), .Y(Y13), .G(G13));
  cores cores_2 (.Sa(s2_1_s2), .Sb(s3_1_s3), .R(R2), .Y(Y2), .G(G2));
  coresp coresp_1 (.S(s4_1_s4), .VM(R45), .VD(G45));

  assign R = G45;
endmodule
